# Fritzing sketch Sketch (saved by Fritzing 0.9.3b)
breadboards: 1

parts:
  Part1 = Bluetooth HC-05 Macho
  L298N1 = L298N DC motor driver
  Part2 = Arduino Nano (Rev3.0)
  1K_Ohms_Brown_Black_Red_Gold1 = Resistor [tolerance=±5% resistance=2k package=THT]
  1K_Ohms_Brown_Black_Red_Gold2 = 1K Ω Resistor [package=THT]
  M1 = DC Motor
  M2 = DC Motor

nets:
  N1: Part1.TXD, Part2.D0/RX
  N2: Part1.RXD, 1K_Ohms_Brown_Black_Red_Gold1.Pin_1, 1K_Ohms_Brown_Black_Red_Gold2.Pin_1
  VCC: Part1.VCC, Part2.5V
  GND: Part1.GND, Part2.GND, 1K_Ohms_Brown_Black_Red_Gold1.Pin_0
  N3: L298N1.OUT1, M2.pin_2
  N4: L298N1.OUT4, M1.pin_2
  N5: L298N1.ENA, Part2.D9
  N6: L298N1.ENB, Part2.D10
  N7: L298N1.IN1, Part2.D4
  N8: L298N1.IN2, Part2.D5
  N9: L298N1.IN3, Part2.D6
  N10: L298N1.IN4, Part2.D7
  N11: Part2.D1/TX, 1K_Ohms_Brown_Black_Red_Gold2.Pin_0

notes:
  9.6V Nimh 2400mAh
  + -

custom parts:
  L298N DC motor driver: 2x DC motor driver with 78M05 positive voltage regulator (7..35 V) L298N: max 46 V, 2 A Set 5 V Enable jumper to enable 5 V regultor (needed for the L298N) and +5 V output at screw terminal or supply external +5 V at screw terminal Set ENA and/or ENB to +5 V to enable motor permanently or supply ENA and/or ENB with PWM signal IN1 and IN2 set rotation directory for motor A (OUT1/OUT2) IN2 and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
  1K Ω Resistor: A generic resistor (0.25W)
